# Fritzing sketch MOS (saved by Fritzing 0.9.10b)

parts:
  M1 = hcmmodu0083 [package=THT]
  OLED_I2C1 = OLED 128x64 I2C Monochrome Display
  元件1 = Arduino Ethernet Shield (Rev3)

nets:
  GND: M1.pin4, OLED_I2C1.GND, 元件1.GND
  N1: M1.pin5, 元件1.PWM_D3
  N2: M1.pin6, OLED_I2C1.SCK, 元件1.A5/SCL
  N3: OLED_I2C1.SDA, 元件1.A4/SDA
  VDD: OLED_I2C1.VDD, 元件1.5V

custom parts:
  hcmmodu0083: hcmmodu0083 IRF540 Mosfet driver module
