# Fritzing sketch 一层货架示意图 (saved by Fritzing 0.9.10b)
breadboards: 1

parts:
  Part2 = Arduino Uno (Rev3)
  Part3 = Adafruit TCA9548A
  OLED_I2C1 = OLED 128x64 I2C Monochrome Display
  Part4 = Arduino Uno (Rev3)
  Part5 = Arduino Uno (Rev3)
  Part6 = Arduino Uno (Rev3)
  OLED_I2C2 = OLED 128x64 I2C Monochrome Display
  OLED_I2C3 = OLED 128x64 I2C Monochrome Display

nets:
  N1: Part2.A4/SDA, Part3.INPUTSDA, Part4.A4/SDA, Part5.A4/SDA, Part6.A4/SDA
  N2: Part2.A5/SCL, Part3.INPUTSCL, Part4.A5/SCL, Part5.A5/SCL, Part6.A5/SCL
  N3: Part2.D7, Part3.RESET
  GND: Part2.GND, Part3.GND, OLED_I2C1.GND, Part4.GND, Part5.GND, Part6.GND, OLED_I2C2.GND, OLED_I2C3.GND
  VIN: Part2.VIN, Part3.VCC, OLED_I2C1.VDD, Part4.VIN, Part5.VIN, Part6.VIN, OLED_I2C2.VDD, OLED_I2C3.VDD
  N4: Part3.2SDA, OLED_I2C3.SDA
  N5: Part3.2SCL, OLED_I2C3.SCK
  N6: Part3.4SCL, OLED_I2C2.SDA
  N7: Part3.5SDA, OLED_I2C2.SCK
  N8: Part3.7SDA, OLED_I2C1.SDA
  N9: Part3.7SCL, OLED_I2C1.SCK

custom parts:
  Adafruit TCA9548A: You just found the perfect I2C sensor, and you want to wire up two or three or more of them to your Arduino when you realize "Uh oh, this chip has a fixed I2C address, and from what I know about I2C, you cannot have two devices with the same address on the same SDA/SCL pins!" Are you out of luck? You would be, if you didn't have this ultra-cool TCA9548A 1-to-8 I2C multiplexer! Finally, a way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
